# Fritzing sketch Smart room controller mid term (saved by Fritzing 1.0.2b)
breadboards: 1

parts:
  A1 = Particle - Photon2
  Part1 = 12 NeoPixel Ring [part_number=1643]
  OLED_I2C1 = OLED 128x64 I2C Monochrome Display
  S1 = Pushbutton [package="[THT]"]
  Part2 = KY-015 Temperature & Humidity Sensor Module [package="Breakout board"]
  M1 = BMP280

nets (from the breadboard view):
  VIN: A1.Pin_2, A1.Pin_8, A1.Pin_31, OLED_I2C1.VDD, S1.Pin_1, S1.Pin_2, Part2.Vin, M1.VIN
  GND: A1.Pin_4, A1.Pin_32, Part1.GND, OLED_I2C1.GND, Part2.-, M1.GND
  N1: A1.Pin_17, OLED_I2C1.SCK, M1.SCL
  N2: A1.Pin_18, OLED_I2C1.SDA, M1.SDA
  N3: A1.Pin_19, Part1.IN
  N4: A1.Pin_21, Part2.S
  N5: A1.Pin_26, Part1.VDD
  N6: S1.Pin_3, S1.Pin_4

custom parts:
  Particle - Photon2: The Photon 2 is a microcontroller and Wi-Fi networking developed by particle. Features: 802.11a/b/g/n Wi-Fi, 2.4 GHz and 5 GHz Integrated PCB antenna Integrated U.FL connector for external antenna Integrated RF switch BLE 5 using same antenna as Wi-Fi Realtek RTL8721DM MCU ARM Cortex M33 CPU, 200 MHz 2048 KB (2 MB) user application maximum size 3072 KB (3 MB) of RAM available to user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
  12 NeoPixel Ring: 12 ultra bright smart LED NeoPixels are arranged in a circle with 1.5" (37mm) outer diameter. The rings are 'chainable' - connect the output pin of one to the input pin of another. Use only one microcontroller pin to control as many as you can chain together! Each LED is addressable as the driver chip is inside the LED. Each one has ~18mA constant current drive so the color will be very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
  Pushbutton: A generic pushbutton.
  KY-015 Temperature & Humidity Sensor Module: KY-015 temperature and humidity sensor module, provides a low-latency serial interface to measure humidity and temperature.
  BMP280: Temperature Humidity Barometric presure Sensor, I2C
